// Digital circuit 5BitALU.dig as structural Verilog
module _5BitALU (
  input  [4:0] A_4_0,
  input  [4:0] B_4_0,
  input  [1:0] OP_1_0,
  output [4:0] R_4_0
);

  wire [4:0] _5bitor_1_r_4_0, _5bitshl_1_r_4_0, adder_1_r_4_0;

  adder adder_1 (.X_4_0(A_4_0), .Y_4_0(B_4_0), .R_4_0(adder_1_r_4_0));  // open: Cout
  _5bitSHL _5bitshl_1 (.A_4_0(A_4_0), .B_4_0(B_4_0), .R_4_0(_5bitshl_1_r_4_0));
  _5bitOR _5bitor_1 (.A_4_0(A_4_0), .B_4_0(B_4_0), .R_4_0(_5bitor_1_r_4_0));
  Multiplexer #(.Selector_Bits(2), .Bits(5)) multiplexer_1 (
    .sel(OP_1_0), .in_0(adder_1_r_4_0), .in_1(_5bitshl_1_r_4_0), .in_2(_5bitor_1_r_4_0), .in_3({5{1'b0}}),
    .out(R_4_0));

  // Other names for the same wires on the sheet: A[4:0] = A_4_0; B[4:0] = B_4_0
endmodule
