// Digital circuit 5BitReg.dig as structural Verilog
module _5BitReg (
  input  [4:0] Din_4_0,
  input  Sel,
  input  CLK,
  output [4:0] Dout
);

  _1bitReg _1bitreg_1 (.Din(Din_4_0[4]), .Sel(Sel), .CLK(CLK), .Dout(Dout[4]));
  _1bitReg _1bitreg_2 (.Din(Din_4_0[3]), .Sel(Sel), .CLK(CLK), .Dout(Dout[3]));
  _1bitReg _1bitreg_3 (.Din(Din_4_0[2]), .Sel(Sel), .CLK(CLK), .Dout(Dout[2]));
  _1bitReg _1bitreg_4 (.Din(Din_4_0[1]), .Sel(Sel), .CLK(CLK), .Dout(Dout[1]));
  _1bitReg _1bitreg_5 (.Din(Din_4_0[0]), .Sel(Sel), .CLK(CLK), .Dout(Dout[0]));

  // Other names for the same wires on the sheet: B0 = Dout[0]; B1 = Dout[1]; B2 = Dout[2]; B3 = Dout[3]; B4 = Dout[4];
  //   A0 = Din_4_0[0]; A1 = Din_4_0[1]; A2 = Din_4_0[2]; A3 = Din_4_0[3]; A4 = Din_4_0[4]
endmodule
