// Digital circuit 5BitRegSetwith3Reg.dig as structural Verilog
module _5BitRegSetwith3Reg (
  input  [1:0] WR_1_0,
  input  WE,
  input  [4:0] WRD_4_0,
  input  CLK,
  input  [1:0] Ra_1_0,
  input  [1:0] Rb_1_0,
  output [4:0] A_4_0,
  output [4:0] B_4_0
);

  wire A0, A1, A2, D0, D1, D2, decoder_1_out_3;
  wire [4:0] R0, R1, R2;

  and and_1 (D1, A1, WE);
  Decoder #(.Selector_Bits(2)) decoder_1 (.sel(WR_1_0), .out_0(A0), .out_1(A1), .out_2(A2), .out_3(decoder_1_out_3));
  and and_2 (D2, A2, WE);
  and and_3 (D0, A0, WE);
  _5BitReg _5bitreg_1 (.Din_4_0(WRD_4_0), .Sel(D2), .CLK(CLK), .Dout(R2));
  _5BitReg _5bitreg_2 (.Din_4_0(WRD_4_0), .Sel(D1), .CLK(CLK), .Dout(R1));
  _5BitReg _5bitreg_3 (.Din_4_0(WRD_4_0), .Sel(D0), .CLK(CLK), .Dout(R0));
  Multiplexer #(.Selector_Bits(2), .Bits(5)) multiplexer_1 (
    .sel(Ra_1_0), .in_0(R0), .in_1(R1), .in_2(R2), .in_3({5{1'b0}}), .out(A_4_0));
  Multiplexer #(.Selector_Bits(2), .Bits(5)) multiplexer_2 (
    .sel(Rb_1_0), .in_0(R0), .in_1(R1), .in_2(R2), .in_3({5{1'b0}}), .out(B_4_0));
  // also tied to GND on the sheet: decoder_1_out_3

  // Other names for the same wires on the sheet: WRD[4:0] = WRD_4_0
endmodule
