// Digital circuit 5bitCPU.dig as structural Verilog
module _5bitCPU (
  input  [17:0] WRD_17_0,
  input  [3:0] WR_3_0,
  input  WE,
  input  CLK,
  input  PC_EN,
  input  [3:0] RA2,
  input  [3:0] ZF,
  output [17:0] RD2_17_0,
  output [4:0] R
);

  wire CPU_CLK, Imm_Sel, JMP_Sel, REG_EN;
  wire [1:0] OP;
  wire [3:0] _4bit_pc_adder_1_o_3_0, _4bit_prog_counter_1_o_3_0, multiplexer_1_out;
  wire [3:2] JMP_Addr;
  wire [4:0] _5bitregsetwith3reg_1_a_4_0, _5bitregsetwith3reg_1_b_4_0, multiplexer_2_out;
  wire [4:3] Imm_Value;
  wire [9:0] Don_t_Care;
  wire [17:14] _9x18ram_1_rd1_17_0;

  Multiplexer #(.Bits(4)) multiplexer_1 (
    .sel(JMP_Sel), .in_0(_4bit_pc_adder_1_o_3_0), .in_1({JMP_Addr, Imm_Value}), .out(multiplexer_1_out));
  _4bit_PC_adder _4bit_pc_adder_1 (.I_3_0(_4bit_prog_counter_1_o_3_0), .O_3_0(_4bit_pc_adder_1_o_3_0));
  _4Bit_Prog_Counter _4bit_prog_counter_1 (
    .I_3_0(multiplexer_1_out), .CLK(CPU_CLK), .O_3_0(_4bit_prog_counter_1_o_3_0));
  and and_1 (CPU_CLK, PC_EN, CLK);
  _9X18RAM _9x18ram_1 (
    .RA1_3_0(_4bit_prog_counter_1_o_3_0), .RA2_3_0(RA2), .WR_3_0(WR_3_0), .WRD_17_0(WRD_17_0), .WE(WE),
    .CLK(CLK), .RD1_17_0({_9x18ram_1_rd1_17_0, JMP_Addr, Imm_Value, Don_t_Care}), .RD2_17_0(RD2_17_0));
  _5bit_CU _5bit_cu_1 (
    .Opcode_3_0(_9x18ram_1_rd1_17_0), .ZF(ZF), .Op(OP), .Reg_EN(REG_EN), .Imm_Sel(Imm_Sel), .Jmp_Sel(JMP_Sel));
  _5BitRegSetwith3Reg _5bitregsetwith3reg_1 (
    .WR_1_0(JMP_Addr), .CLK(CPU_CLK), .WE(REG_EN), .WRD_4_0(R), .A_4_0(_5bitregsetwith3reg_1_a_4_0),
    .B_4_0(_5bitregsetwith3reg_1_b_4_0), .Ra_1_0(JMP_Addr), .Rb_1_0(Imm_Value));
  _5BitALU _5bitalu_1 (.A_4_0(_5bitregsetwith3reg_1_a_4_0), .B_4_0(multiplexer_2_out), .OP_1_0(OP), .R_4_0(R));
  Multiplexer #(.Bits(5)) multiplexer_2 (
    .sel(Imm_Sel), .in_0(_5bitregsetwith3reg_1_b_4_0), .in_1({Imm_Value, Don_t_Care[9:7]}),
    .out(multiplexer_2_out));
  // Pins of 1 and 4 bits meet at ZF

  // Other names for the same wires on the sheet: Imm_Value[2:0] = Don_t_Care[9:7]; JMP_Addr[1:0] = Imm_Value;
  //   RD2[17:0] = RD2_17_0

  // Notes on the sheet:
  //   Register mode(type of op=00)= 2bit (type of op)+2bit (op) + 2bit (Reg1) + 2bit (Reg2) + 10bit (Don't Care)
  //   Immediate mode(Type of op=01)=2bit (type of op) + 2bit (op) + 2bit (Reg1) + 5bit (Imm  value) + 7bit (Don't Care)
  //   Jump mode(Type of op=10)=2bit (type of op) + 2bit (op) + 4bit (Addr) + 10bit (Don't Care)
  //   Add(Op=00), Shift Left(Op=01), OR(Op=10)
  //   JMP(Op=00), JL(Op=01)
  //   JL START		100100010000000000
  //   START: ADD R0,R1	000000010000000000
  //   JMPTO: ADD R0,5	010000001010000000
  //   JMP JMPTO		100000100000000000
endmodule
