// Digital circuit adder.dig as structural Verilog
module adder (
  input  [4:0] X_4_0,
  input  [4:0] Y_4_0,
  output [4:0] R_4_0,
  output Cout
);

  wire fa_2_cout, fa_3_cout, fa_4_cout, fa_5_cout;

  FA fa_1 (.X(X_4_0[4]), .Y(Y_4_0[4]), .Cin(fa_2_cout), .S(R_4_0[4]), .Cout(Cout));
  FA fa_2 (.X(X_4_0[3]), .Y(Y_4_0[3]), .Cin(fa_3_cout), .S(R_4_0[3]), .Cout(fa_2_cout));
  FA fa_3 (.X(X_4_0[2]), .Y(Y_4_0[2]), .Cin(fa_4_cout), .S(R_4_0[2]), .Cout(fa_3_cout));
  FA fa_4 (.X(X_4_0[1]), .Y(Y_4_0[1]), .Cin(fa_5_cout), .S(R_4_0[1]), .Cout(fa_4_cout));
  FA fa_5 (.X(X_4_0[0]), .Y(Y_4_0[0]), .Cin(1'b0), .S(R_4_0[0]), .Cout(fa_5_cout));
endmodule
